// Logisim project s-mips.circ as structural Verilog
module S_MIPS_Board (
  input  DESHABILITAR_DISPATCHER,
  output halt
);

  wire button_1_out, CLK, CS, d_ff_1_q, LCLR, LoadRAM, LoadRAMOn, LW, R_R_W, R_W, ram_dispatcher_1_finished,
       RCS, Reset_out, RST, TTY_EN;
  wire [2:0] KDB;
  wire [3:0] LMask, Mask, ram_1_read_time, ram_1_write_time, RMask;
  wire [6:0] KDB_DATA, TTY_DATA;
  wire [15:0] Addr, LAddr, RAddr;
  wire [31:0] I0, I1, I2, I3, LData, ram_1_data_out_0, ram_1_data_out_1, ram_1_data_out_2, ram_1_data_out_3,
       RI0, RI1, RI2, RI3;

  TTY #(.rows(25), .cols(80)) tty_1 (.data(TTY_DATA), .clk(CLK), .we(TTY_EN), .clr(RST));
  not not_1 (LoadRAMOn, ram_dispatcher_1_finished);
  RAM_Dispatcher ram_dispatcher_1 (
    .WriteTime(ram_1_write_time), .Clock(CLK), .Data(LData), .Address(LAddr), .Mask(LMask),
    .Finished(ram_dispatcher_1_finished), .Write(LW), .CLR(LCLR));
  Keyboard #(.buflen(64)) keyboard_1 (.clk(CLK), .re(KDB[0]), .avail(KDB[2]), .data(KDB_DATA));  // open: clr
  RAM ram_1 (
    .Address(RAddr), .Data_Out_0(ram_1_data_out_0), .Data_Out_1(ram_1_data_out_1),
    .Data_Out_2(ram_1_data_out_2), .Data_Out_3(ram_1_data_out_3), .Data_In_0(RI0), .Data_In_1(RI1),
    .Data_In_2(RI2), .Data_In_3(RI3), .Mask(RMask), .nRead_Write(R_R_W), .Chip_Select(RCS),
    .Read_Time(ram_1_read_time), .Reset(button_1_out), .Write_Time(ram_1_write_time));
  Button button_1 (.out(button_1_out));
  D_Flip_Flop d_ff_1 (.clk(CLK), .D(1'b1), .Q(d_ff_1_q), .reset(Reset_out));  // open: Qn, preset, en
  Button Reset (.out(Reset_out));
  S_MIPS s_mips_1 (
    .Kbd_Enable(KDB[0]), .Address(Addr), .Kbd_Clear(KDB[1]), .Kbd_Available(KDB[2]), .RAM_In_0(I0),
    .Kbd_ASCII_Data(KDB_DATA), .RAM_In_1(I1), .TTY_Enable(TTY_EN), .RAM_In_2(I2), .RAM_In_3(I3),
    .TTY_ASCII_Data(TTY_DATA), .Reset(RST), .RAM_Out_0(ram_1_data_out_0), .Clock(CLK),
    .RAM_Out_1(ram_1_data_out_1), .Stop(halt), .RAM_Out_2(ram_1_data_out_2), .RAM_Out_3(ram_1_data_out_3),
    .Mask(Mask), .Read_Time(ram_1_read_time), .Write_Time(ram_1_write_time), .nRead_Write(R_W),
    .Chip_Select(CS));
  D_Flip_Flop d_ff_2 (.clk(CLK), .D(d_ff_1_q), .Qn(LCLR), .reset(Reset_out));  // open: Q, preset, en
  or or_1 (RST, LCLR, LoadRAM);
  Clock clock_1 (.out(CLK));
  Multiplexer #(.width(32), .enable("false")) multiplexer_1 (.in0(I0), .in1(LData), .out(RI0), .sel(LoadRAM));
  Multiplexer #(.width(32), .enable("false")) multiplexer_2 (.in0(I1), .in1(LData), .out(RI1), .sel(LoadRAM));
  Multiplexer #(.width(32), .enable("false")) multiplexer_3 (.in0(I2), .in1(LData), .out(RI2), .sel(LoadRAM));
  Multiplexer #(.width(32), .enable("false")) multiplexer_4 (.in0(I3), .in1(LData), .out(RI3), .sel(LoadRAM));
  and and_1 (LoadRAM, ~DESHABILITAR_DISPATCHER, LoadRAMOn);  // AND_Gate
  Multiplexer #(.width(16), .enable("false")) multiplexer_5 (.in0(Addr), .in1(LAddr), .out(RAddr), .sel(LoadRAM));
  Multiplexer #(.width(4), .enable("false")) multiplexer_6 (.in0(Mask), .in1(LMask), .out(RMask), .sel(LoadRAM));
  Multiplexer #(.enable("false")) multiplexer_7 (.in0(CS), .in1(LW), .out(RCS), .sel(LoadRAM));
  Multiplexer #(.enable("false")) multiplexer_8 (.in0(R_W), .in1(LW), .out(R_R_W), .sel(LoadRAM));

  // Notes on the sheet:
  //   NO MODIFICAR
  //   Keyboard
endmodule

module RAM (
  input  [15:0] Address,
  input  [31:0] Data_In_0,
  input  [31:0] Data_In_1,
  input  [31:0] Data_In_2,
  input  [31:0] Data_In_3,
  input  [3:0] Mask,
  input  nRead_Write,
  input  Chip_Select,
  input  Reset,
  output [31:0] Data_Out_0,
  output [31:0] Data_Out_1,
  output [31:0] Data_Out_2,
  output [31:0] Data_Out_3,
  output [3:0] Read_Time,
  output [3:0] Write_Time
);

  wire and_2_out, and_3_out, and_4_out, and_5_out, and_6_out, and_7_out, and_8_out, and_9_out, Changed, CLK,
       comparator_2_eq, comparator_3_eq, comparator_4_eq, comparator_5_eq, comparator_6_eq, Count,
       demultiplexer_3_out0, Idle, Idle_q, Load, Load0, Load1, nand_1_out, or_1_out, or_2_out, or_3_out,
       or_4_out, or_5_out, or_6_out, or_7_out, or_8_out, or_9_out, or_10_out, Proc_q, Update_Mem, Zero_Time;
  wire [3:0] counter_1_q, multiplexer_1_out, subtractor_1_out;
  wire [31:0] register_1_q, register_2_q, register_3_q, register_4_q, register_5_q;

  // Probe on 4'b0011
  // Probe on 4'b0010
  Multiplexer #(.width(4), .enable("false")) multiplexer_1 (
    .in0(4'b0011), .in1(4'b0010), .out(multiplexer_1_out), .sel(nRead_Write));
  or or_1 (or_1_out, Idle, Update_Mem);
  or or_2 (or_2_out, ~Chip_Select, Reset);  // OR_Gate
  Subtractor #(.width(4)) subtractor_1 (.a(multiplexer_1_out), .b(4'b0010), .out(subtractor_1_out));  // open: bin, bout
  Demultiplexer #(.enable("false")) demultiplexer_1 (.out0(Idle), .out1(Load0), .in(Idle_q), .sel(Changed));
  D_Flip_Flop u_Idle (.clk(CLK), .D(or_1_out), .Q(Idle_q), .preset(or_2_out));  // open: Qn, en, reset
  // Probe on counter_1_q
  Counter #(.width(4), .max('hf)) counter_1 (
    .load(Load), .D(subtractor_1_out), .count(Count), .Q(counter_1_q), .clk(CLK), .clr(or_3_out));  // open: carry
  or or_3 (or_3_out, ~Chip_Select, Reset);  // OR_Gate
  Comparator #(.width(4), .mode("unsigned")) comparator_1 (
    .a(4'b0000), .b(counter_1_q), .eq(Zero_Time));  // open: gt, lt
  or or_4 (or_4_out, Count, Load0, Load1);
  Register #(.width(32)) register_1 (.D(Data_In_0), .en(Chip_Select), .Q(register_1_q), .clk(CLK), .clr(or_5_out));
  or or_5 (or_5_out, ~Chip_Select, Reset);  // OR_Gate
  Register #(.width(32)) register_2 (.D(Data_In_1), .en(Chip_Select), .Q(register_2_q), .clk(CLK), .clr(or_6_out));
  or or_6 (or_6_out, ~Chip_Select, Reset);  // OR_Gate
  Register #(.width(32)) register_3 (.D(Data_In_2), .en(Chip_Select), .Q(register_3_q), .clk(CLK), .clr(or_7_out));
  or or_7 (or_7_out, ~Chip_Select, Reset);  // OR_Gate
  Register #(.width(32)) register_4 (.D(Data_In_3), .en(Chip_Select), .Q(register_4_q), .clk(CLK), .clr(or_8_out));
  or or_8 (or_8_out, ~Chip_Select, Reset);  // OR_Gate
  Register #(.width(32)) register_5 (
    .D({{11{1'b1}}, nRead_Write, Mask, Address}), .en(Chip_Select), .Q(register_5_q), .clk(CLK),
    .clr(or_9_out));
  or or_9 (or_9_out, ~Chip_Select, Reset);  // OR_Gate
  D_Flip_Flop Proc (.clk(CLK), .D(or_4_out), .Q(Proc_q), .reset(or_10_out));  // open: Qn, preset, en
  or or_10 (or_10_out, ~Chip_Select, Reset);  // OR_Gate
  Demultiplexer #(.enable("false")) demultiplexer_2 (
    .out0(Count), .out1(Update_Mem), .in(demultiplexer_3_out0), .sel(Zero_Time));
  Demultiplexer #(.enable("false")) demultiplexer_3 (
    .out0(demultiplexer_3_out0), .out1(Load1), .in(Proc_q), .sel(Changed));
  Clock clock_1 (.out(CLK));
  Comparator #(.width(32)) comparator_2 (.a(register_1_q), .b(Data_In_0), .eq(comparator_2_eq));  // open: gt, lt
  Comparator #(.width(32)) comparator_3 (.a(register_2_q), .b(Data_In_1), .eq(comparator_3_eq));  // open: gt, lt
  Comparator #(.width(32)) comparator_4 (.a(register_3_q), .b(Data_In_2), .eq(comparator_4_eq));  // open: gt, lt
  Comparator #(.width(32)) comparator_5 (.a(register_4_q), .b(Data_In_3), .eq(comparator_5_eq));  // open: gt, lt
  Comparator #(.width(32)) comparator_6 (
    .a(register_5_q), .b({{11{1'b1}}, nRead_Write, Mask, Address}), .eq(comparator_6_eq));  // open: gt, lt
  nand nand_1 (nand_1_out, comparator_6_eq, comparator_2_eq, comparator_3_eq, comparator_4_eq, comparator_5_eq);
  and and_1 (Changed, nand_1_out, Chip_Select);
  or or_11 (Load, Count, Load1, Load0);
  and and_2 (and_2_out, Mask[0], Update_Mem, nRead_Write);
  and and_3 (and_3_out, Mask[1], Update_Mem, nRead_Write);
  and and_4 (and_4_out, Mask[2], Update_Mem, nRead_Write);
  and and_5 (and_5_out, Mask[3], Update_Mem, nRead_Write);
  RAM_part #(.addrWidth(16), .dataWidth(32), .bus("separate")) ram_1 (
    .addr(Address), .din(Data_In_0), .data(Data_Out_0), .str(and_2_out), .sel(Chip_Select), .clk(CLK),
    .ld(and_6_out), .clr(Reset));
  and and_6 (and_6_out, ~nRead_Write, Idle);  // AND_Gate
  RAM_part #(.addrWidth(16), .dataWidth(32), .bus("separate")) ram_2 (
    .addr(Address), .din(Data_In_1), .data(Data_Out_1), .str(and_3_out), .sel(Chip_Select), .clk(CLK),
    .ld(and_7_out), .clr(Reset));
  and and_7 (and_7_out, ~nRead_Write, Idle);  // AND_Gate
  RAM_part #(.addrWidth(16), .dataWidth(32), .bus("separate")) ram_3 (
    .addr(Address), .din(Data_In_2), .data(Data_Out_2), .str(and_4_out), .sel(Chip_Select), .clk(CLK),
    .ld(and_8_out), .clr(Reset));
  and and_8 (and_8_out, ~nRead_Write, Idle);  // AND_Gate
  RAM_part #(.addrWidth(16), .dataWidth(32), .bus("separate")) ram_4 (
    .addr(Address), .din(Data_In_3), .data(Data_Out_3), .str(and_5_out), .sel(Chip_Select), .clk(CLK),
    .ld(and_9_out), .clr(Reset));
  and and_9 (and_9_out, ~nRead_Write, Idle);  // AND_Gate

  assign Read_Time = 4'b0011;
  assign Write_Time = 4'b0010;

  // Other names for the same wires on the sheet: M0 = Mask[0]; M1 = Mask[1]; M2 = Mask[2]; M3 = Mask[3];
  //   RW = nRead_Write; CLR = Reset; CS = Chip_Select; Load2 = Count

  // Notes on the sheet:
  //   NO MODIFICAR
  //   excepto quizás los valores RT y WT
  //   BANK0
  //   BANK1
  //   BANK2
  //   BANK3
endmodule

module S_MIPS (
  input  Reset,
  input  [3:0] Read_Time,
  input  [31:0] RAM_Out_0,
  input  Clock,
  input  [3:0] Write_Time,
  input  Kbd_Available,
  input  [6:0] Kbd_ASCII_Data,
  input  [31:0] RAM_Out_1,
  input  [31:0] RAM_Out_2,
  input  [31:0] RAM_Out_3,
  output Kbd_Enable,
  output [31:0] RAM_In_0,
  output Kbd_Clear,
  output Stop,
  output [31:0] RAM_In_1,
  output [15:0] Address,
  output TTY_Enable,
  output [31:0] RAM_In_2,
  output [6:0] TTY_ASCII_Data,
  output nRead_Write,
  output Chip_Select,
  output [31:0] RAM_In_3,
  output [3:0] Mask
);

  wire control_unit_1_load_instruction, control_unit_1_load_pc, control_unit_1_logical_inmed_op,
       control_unit_1_r_w, control_unit_1_rt_rd, datapath_1_nf, datapath_1_zf, pop, push, Save_Data;
  wire [1:0] control_unit_1_select_b, Slct_Address;
  wire [2:0] Branch_Op, control_unit_1_select_di;
  wire [3:0] control_unit_1_alu_op;
  wire [4:0] instruction_decoder_1_da, instruction_decoder_1_sa, instruction_decoder_1_sb;
  wire [5:0] Func_Code, Op_Code;
  wire [15:0] instruction_decoder_1_offset;
  wire [25:0] address_t;
  wire [31:0] add_lw_sw, Data_In, datapath_1_const, From_PC, multiplexer_1_out, multiplexer_2_out, RT, SP,
       To_PC;
  wire [31:7] RS;

  Multiplexer #(.select(2), .width(32), .enable("false")) multiplexer_1 (
    .in0(From_PC), .in1(add_lw_sw), .in2(SP), .out(multiplexer_1_out), .sel(Slct_Address));  // open: in3
  Multiplexer #(.width(32), .enable("false")) multiplexer_2 (
    .in0(RT), .in1({RS, TTY_ASCII_Data}), .out(multiplexer_2_out), .sel(push));
  RAM_Manager_2 ram_manager_1 (
    .in_1(multiplexer_1_out), .clk(Clock), .save_data(Save_Data), .rst(Reset), .RAM_O0(RAM_Out_0),
    .RAM_O1(RAM_Out_1), .RAM_In(multiplexer_2_out), .RAM_O2(RAM_Out_2), .RAM_O3(RAM_Out_3), .Mask(Mask),
    .Address_Out(Address), .RAM_O0_2(RAM_In_0), .RAM_O1_2(RAM_In_1), .RAM_Out(Data_In), .RAM_O2_2(RAM_In_2),
    .RAM_O3_2(RAM_In_2));
  Control_Unit_2 control_unit_1 (
    .Op_code(Op_Code), .Func_code(Func_Code), .Read_Time(Read_Time), .Write_Time(Write_Time), .CLK(Clock),
    .Reset(Reset), .ALU_Op(control_unit_1_alu_op), .Branch_Op(Branch_Op),
    .Logical_Inmed_Op(control_unit_1_logical_inmed_op), .Select_DI(control_unit_1_select_di), .pop(pop),
    .KBD_ENABLE(Kbd_Enable), .TTY_ENABLE(TTY_Enable), .Chip_Select(Chip_Select), .RW_RAM(nRead_Write),
    .Load_PC(control_unit_1_load_pc), .Load_Instruction(control_unit_1_load_instruction),
    .R_W(control_unit_1_r_w), .rt_rd(control_unit_1_rt_rd), .Select_B(control_unit_1_select_b),
    .Select_Address(Slct_Address), .Push(push), .Save_Data(Save_Data), .END(Stop));
  Instruction_Decoder_2 instruction_decoder_1 (
    .Load_Inst(control_unit_1_load_instruction), .Clock(Clock), .Reset(Reset), .DA(instruction_decoder_1_da),
    .Address(address_t), .SA(instruction_decoder_1_sa), .offset(instruction_decoder_1_offset),
    .SB(instruction_decoder_1_sb), .Func_code(Func_Code), .Op_code(Op_Code), .Instruction(Data_In));
  Datapath datapath_1 (
    .Data(Data_In), .clk(Clock), .reset(Reset), .write_PC(control_unit_1_load_pc),
    .select_B(control_unit_1_select_b), .ALU_Op(control_unit_1_alu_op), .Select_DI(control_unit_1_select_di),
    .Logical_Inmed_Op(control_unit_1_logical_inmed_op), .R_W(control_unit_1_r_w),
    .rt_rd(control_unit_1_rt_rd), .Push(push), .Pop(pop), .RS(instruction_decoder_1_sa),
    .RT(instruction_decoder_1_sb), .RD(instruction_decoder_1_da), .Offset(instruction_decoder_1_offset),
    .To_PC(To_PC), .KBD_Available(Kbd_Available), .KBD_Data(Kbd_ASCII_Data), .RT_2(RT),
    .add_lw_sw(add_lw_sw), .SP(SP), .From_PC(From_PC), .RS_2({RS, TTY_ASCII_Data}), .Const(datapath_1_const),
    .ZF(datapath_1_zf), .NF(datapath_1_nf));
  Branch_Control_2 branch_control_1 (
    .PC_in(From_PC), .RS({RS, TTY_ASCII_Data}), .\const (datapath_1_const), .Jump(address_t),
    .Branch_Op(Branch_Op), .ZF(datapath_1_zf), .NF(datapath_1_nf), .PC_Out(To_PC));

  assign Kbd_Clear = Reset;
  assign RAM_In_3 = RAM_In_2;

  // Other names for the same wires on the sheet: CLK = Clock; CS = Chip_Select; KBD_AVAIL = Kbd_Available;
  //   CLR = Reset; KBD_CLR = Reset; KBD_DATA[6:0] = Kbd_ASCII_Data; RAM_A[15:0] = Address;
  //   RAM_INPUT_0[31:0] = RAM_In_0; RAM_INPUT_1[31:0] = RAM_In_1; RAM_INPUT_2[31:0] = RAM_In_2;
  //   RAM_INPUT_3[31:0] = RAM_In_2; RAM_MASK[3:0] = Mask; RAM_OUTPUT_0[31:0] = RAM_Out_0;
  //   RAM_OUTPUT_1[31:0] = RAM_Out_1; RAM_OUTPUT_2[31:0] = RAM_Out_2; RAM_OUTPUT_3[31:0] = RAM_Out_3;
  //   RS[6:0] = TTY_ASCII_Data; TTY_DATA[6:0] = TTY_ASCII_Data; RW = nRead_Write

  // Notes on the sheet:
  //   Inputs RAM
  //   DATA FROM RAM
  //   DATA WRITE MASK
  //   Outputs RAM
  //   RAM TIMING
  //   RAM ADDRESS
  //   RAM CONTROL
  //   DATA TO RAM
  //   Utilities
  //   KEYBOARD
  //   SEQUENCING
  //   TTY
endmodule

module RAM_Dispatcher (
  input  [3:0] WriteTime,
  input  Clock,
  input  CLR,
  output [31:0] Data,
  output [15:0] Address,
  output [3:0] Mask,
  output Finished,
  output Write
);

  wire demultiplexer_2_out1, demultiplexer_3_out1, End, IDLE_q, IncAddr, Load, or_1_out, or_2_out, While_q,
       WriteEnd;
  wire [3:0] counter_1_q;
  wire [31:0] CurrentAddress_q;

  Counter #(.width(32), .max('hffffffff)) CurrentAddress (
    .count(IncAddr), .Q({CurrentAddress_q[31:18], Address, CurrentAddress_q[1:0]}), .clk(Clock), .clr(CLR));  // open: load, D, carry
  or or_1 (or_1_out, IncAddr, demultiplexer_3_out1, Finished);
  D_Flip_Flop IDLE (.clk(Clock), .D(or_1_out), .Q(IDLE_q), .preset(CLR));  // open: Qn, en, reset
  Demultiplexer #(.enable("false")) demultiplexer_1 (.out0(Load), .out1(Finished), .in(IDLE_q), .sel(End));
  D_Flip_Flop While (.clk(Clock), .D(or_2_out), .Q(While_q), .reset(CLR));  // open: Qn, preset, en
  or or_2 (or_2_out, Write, Load);
  RAM_part #(.addrWidth(18), .dataWidth(32)) ram_1 (
    .addr({Address, CurrentAddress_q[1:0]}), .data(Data), .clk(Clock));  // open: sel, ld, clr
  Demultiplexer #(.enable("false")) demultiplexer_2 (
    .out0(Write), .out1(demultiplexer_2_out1), .in(While_q), .sel(WriteEnd));
  Decoder #(.select(2)) decoder_1 (
    .out0(Mask[0]), .out1(Mask[1]), .out2(Mask[2]), .out3(Mask[3]), .sel(CurrentAddress_q[1:0]));  // open: en
  Demultiplexer #(.enable("false")) demultiplexer_3 (
    .out0(IncAddr), .out1(demultiplexer_3_out1), .in(demultiplexer_2_out1), .sel(End));
  Counter #(.width(4), .max('hf)) counter_1 (
    .load(Load), .D(WriteTime), .count(Write), .Q(counter_1_q), .clk(Clock));  // open: carry, clr
  Comparator #(.width(32)) comparator_1 (.a(Data), .b({32{1'b1}}), .eq(End));  // open: gt, lt
  Comparator #(.width(4)) comparator_2 (.a(4'b0000), .b(counter_1_q), .eq(WriteEnd));  // open: gt, lt

  // Other names for the same wires on the sheet: CLK = Clock; Count = Write; WT[3:0] = WriteTime
endmodule

module Datapath (
  input  write_PC,
  input  Logical_Inmed_Op,
  input  [4:0] RS,
  input  [31:0] Data,
  input  [15:0] Offset,
  input  R_W,
  input  [1:0] select_B,
  input  [4:0] RT,
  input  rt_rd,
  input  [4:0] RD,
  input  clk,
  input  [3:0] ALU_Op,
  input  Push,
  input  reset,
  input  [2:0] Select_DI,
  input  Pop,
  input  [31:0] To_PC,
  input  KBD_Available,
  input  [6:0] KBD_Data,
  output [31:0] RT_2,
  output [31:0] From_PC,
  output [31:0] add_lw_sw,
  output [31:0] RS_2,
  output ZF,
  output [31:0] SP,
  output [31:0] Const,
  output NF
);

  wire and_1_out;
  wire [4:0] multiplexer_3_out;
  wire [31:0] alu_1_hi, alu_1_lo, ALU_Out, bit_extender_1_out, Hi, Lo, multiplexer_1_out, multiplexer_4_out,
       Random_out, RF_In, tunnel, undriven;

  assign bit_extender_1_out = {{25{1'b0}}, KBD_Data};  // Bit_Extender bit_extender_1
  Multiplexer #(.width(32), .enable("false")) multiplexer_1 (
    .in0({32{1'b1}}), .in1(bit_extender_1_out), .out(multiplexer_1_out), .sel(KBD_Available));
  Random #(.width(32), .seed(212)) Random (.clk(clk), .next(1'b1), .out(Random_out), .clr(reset));
  Multiplexer #(.select(3), .width(32), .enable("false")) multiplexer_2 (
    .in0(ALU_Out), .in1(Data), .in2(Hi), .in3(Lo), .in4(multiplexer_1_out), .in5(Random_out), .out(RF_In),
    .sel(Select_DI));  // open: in6, in7
  Register #(.width(32)) PC (.D(To_PC), .en(write_PC), .Q(From_PC), .clk(clk), .clr(reset));
  Multiplexer #(.width(5), .enable("false")) multiplexer_3 (.in0(RT), .in1(RD), .out(multiplexer_3_out), .sel(rt_rd));
  Register_File_2 register_file_1 (
    .in_1(multiplexer_3_out), .in_2(RF_In), .RW(R_W), .SA(RS), .SB(RT), .in_7(reset), .in_9(Pop), .in_6(clk),
    .in_8(Push), .A(RS_2), .B(RT_2), .SP(SP));
  Sing_Extend_2 sing_extend_1 (.in_1(Offset), .Logical(Logical_Inmed_Op), .Output(Const));
  Multiplexer #(.select(2), .width(32), .enable("false")) multiplexer_4 (
    .in0(RT_2), .in1(undriven), .in2(Const), .in3(tunnel), .out(multiplexer_4_out), .sel(select_B));
  ALU_2 alu_1 (
    .A(RS_2), .B(multiplexer_4_out), .ALU(ALU_Op), .Out(ALU_Out), .Zero(ZF), .Neg(NF), .Hi(alu_1_hi),
    .Lo(alu_1_lo));
  and and_1 (and_1_out, ALU_Op[3], ~ALU_Op[2]);  // AND_Gate
  Register #(.width(32)) u_Hi (.D(alu_1_hi), .en(and_1_out), .Q(Hi), .clk(clk), .clr(reset));
  Register #(.width(32)) u_Lo (.D(alu_1_lo), .en(and_1_out), .Q(Lo), .clk(clk), .clr(reset));

  // Other names for the same wires on the sheet: ALU_out_t[31:0] = add_lw_sw; Data_In[31:0] = Data;
  //   KBD_A = KBD_Available; KBD_D[6:0] = KBD_Data; Logical = Logical_Inmed_Op; RS_t[31:0] = RS_2; rst = reset;
  //   RT_t[31:0] = RT_2

  // Notes on the sheet:
  //   Data From RAM
  //   RF Input Selecter
  //   Inputs
  //   CU Sings
  //   Program Counter
  //   From Instruction Decoder
  //   From Branch Control
  //   Data From KBD
  //   Data To RAM
  //   Outputs
  //   Data To RAM
endmodule

module ALU_2 (
  input  [31:0] A,
  input  [31:0] B,
  input  [3:0] ALU,
  output [31:0] Out,
  output Zero,
  output Neg,
  output [31:0] Hi,
  output [31:0] Lo
);

  wire comparator_1_lt, comparator_2_lt;
  wire [31:0] AND, D_Hi, D_Lo, DIV_Hi, DIV_Lo, M_Hi, M_Lo, MULT_Hi, MULT_Lo, NOR, OR, tunnel, tunnel_t,
       tunnel_t_t, tunnel_t_t_t, XOR;

  // Probe on A
  // Probe on B
  Adder #(.width(32)) adder_1 (.a(A), .b(B), .out(tunnel));  // open: cin, cout
  Subtractor #(.width(32)) subtractor_1 (.a(A), .b(B), .out(tunnel_t));  // open: bin, bout
  assign AND = A & B;  // AND_Gate and_1, 32 bits wide
  assign OR = A | B;  // OR_Gate or_1, 32 bits wide
  Multiplier_part #(.width(32)) multiplier_1 (.a(A), .b(B), .out(MULT_Lo), .cout(MULT_Hi));  // open: cin
  // Multiplier multiplier_2: pin names not known; wires that end beside it: A, B, M_Lo
  assign NOR = ~(A | B);  // NOR_Gate nor_1, 32 bits wide
  assign XOR = A ^ B;  // XOR_Gate xor_1, 32 bits wide
  Comparator #(.width(32)) comparator_1 (.a(A), .b(B), .lt(comparator_1_lt));  // open: gt, eq
  Comparator #(.width(32)) comparator_2 (.a(A), .b(B), .lt(comparator_2_lt));  // open: gt, eq
  Divider_part #(.width(32)) divider_1 (.a(A), .b(B), .out(DIV_Lo), .rem(DIV_Hi));  // open: upper
  Divider divider_2 (.A(A), .B(B), .Hi(D_Lo), .Lo(D_Hi));
  Multiplexer #(.width(32), .enable("false")) multiplexer_1 (
    .in0({32{1'b0}}), .in1(32'h1), .out(tunnel_t_t), .sel(comparator_1_lt));
  Multiplexer #(.width(32), .enable("false")) multiplexer_2 (
    .in0({32{1'b0}}), .in1(32'h1), .out(tunnel_t_t_t), .sel(comparator_2_lt));
  Multiplexer #(.select(3), .width(32), .enable("false")) multiplexer_3 (
    .in0(tunnel), .in1(tunnel_t), .in2(AND), .in3(OR), .in4(NOR), .in5(XOR), .in6(tunnel_t_t),
    .in7(tunnel_t_t_t), .out({Neg, Out[30:0]}), .sel(ALU[2:0]));
  Multiplexer #(.select(2), .width(32), .enable("false")) multiplexer_4 (
    .in0(MULT_Hi), .in1(M_Hi), .in2(DIV_Hi), .in3(D_Hi), .out(Hi), .sel(ALU[1:0]));
  Multiplexer #(.select(2), .width(32), .enable("false")) multiplexer_5 (
    .in0(MULT_Lo), .in1(M_Lo), .in2(DIV_Lo), .in3(D_Lo), .out(Lo), .sel(ALU[1:0]));
  // Probe on {Neg, Out[30:0]}
  // Probe on Hi
  // Probe on Lo
  Comparator #(.width(32)) comparator_3 (.a({Neg, Out[30:0]}), .b({32{1'b0}}), .eq(Zero));  // open: gt, lt

  assign Out[31] = Neg;

  // Other names for the same wires on the sheet: O[2:0] = ALU[2:0]; O_Hi_Lo[1:0] = ALU[1:0]

  // Notes on the sheet:
  //   Operand A
  //   Operand B
  //   Inputs
  //   ALU Control
  //   Basic Operations
  //   Hi/Lo Operations
  //   Multiplier
  //   ALU
  //   Adder
  //   Substractor
  //   AND
  //   OR
  //   NOR
  //   XOR
  //   Comparator
  //   Divider
  //   Hi/Lo Outputs
  //   Outputs
  //   Normal
  //   SubCircuits
endmodule

module Multiplier (
  input  [31:0] A,
  input  [31:0] B,
  output [31:0] Hi,
  output [31:0] Lo
);

  wire adder_1_cout, adder_3_cout;
  wire [31:0] _00_Hi, _00_Lo, _01_Hi, _01_Lo, _10_Hi, _10_Lo, _11_Hi, _11_Lo, bit_extender_1_out,
       bit_extender_2_out, multiplier_3_cout, multiplier_3_out, multiplier_4_cout, multiplier_4_out,
       nand_1_out, nand_2_out, nand_3_out, nand_4_out, negator_1_out, negator_2_out, negator_3_out,
       negator_4_out;

  // Probe on A
  // Probe on B
  // Probe on Hi
  Multiplexer #(.select(2), .width(32), .enable("false")) multiplexer_1 (
    .in0(_00_Hi), .in1(_01_Hi), .in2(_10_Hi), .in3(_11_Hi), .out(Hi), .sel({A[31], B[31]}));
  // Probe on Lo
  Multiplexer #(.select(2), .width(32), .enable("false")) multiplexer_2 (
    .in0(_00_Lo), .in1(_01_Lo), .in2(_10_Lo), .in3(_11_Lo), .out(Lo), .sel({A[31], B[31]}));
  Multiplier_part #(.width(32)) multiplier_1 (.a(A), .b(B), .out(_00_Lo), .cout(_00_Hi));  // open: cin
  Negator #(.width(32)) negator_1 (.in(A), .out(negator_1_out));
  Multiplier_part #(.width(32)) multiplier_2 (
    .a(negator_1_out), .b(negator_2_out), .out(_11_Lo), .cout(_11_Hi));  // open: cin
  Negator #(.width(32)) negator_2 (.in(B), .out(negator_2_out));
  Multiplier_part #(.width(32)) multiplier_3 (
    .a(A), .b(negator_3_out), .out(multiplier_3_out), .cout(multiplier_3_cout));  // open: cin
  Negator #(.width(32)) negator_3 (.in(B), .out(negator_3_out));
  Negator #(.width(32)) negator_4 (.in(A), .out(negator_4_out));
  Multiplier_part #(.width(32)) multiplier_4 (
    .a(negator_4_out), .b(B), .out(multiplier_4_out), .cout(multiplier_4_cout));  // open: cin
  assign nand_1_out = ~(multiplier_3_out & {32{1'b1}});  // NAND_Gate nand_1, 32 bits wide
  assign nand_2_out = ~(multiplier_3_cout & {32{1'b1}});  // NAND_Gate nand_2, 32 bits wide
  assign nand_3_out = ~(multiplier_4_out & {32{1'b1}});  // NAND_Gate nand_3, 32 bits wide
  assign nand_4_out = ~(multiplier_4_cout & {32{1'b1}});  // NAND_Gate nand_4, 32 bits wide
  assign bit_extender_1_out = {{31{1'b0}}, adder_1_cout};  // Bit_Extender bit_extender_1
  assign bit_extender_2_out = {{31{1'b0}}, adder_3_cout};  // Bit_Extender bit_extender_2
  Adder #(.width(32)) adder_1 (.a(nand_1_out), .b(32'h1), .out(_01_Lo), .cout(adder_1_cout));  // open: cin
  Adder #(.width(32)) adder_2 (.a(nand_2_out), .b(bit_extender_1_out), .out(_01_Hi));  // open: cin, cout
  Adder #(.width(32)) adder_3 (.a(nand_3_out), .b(32'h1), .out(_10_Lo), .cout(adder_3_cout));  // open: cin
  Adder #(.width(32)) adder_4 (.a(nand_4_out), .b(bit_extender_2_out), .out(_10_Hi));  // open: cin, cout

  // Other names for the same wires on the sheet: A_t = A[31]; B_t = B[31]

  // Notes on the sheet:
  //   Operand A
  //   Operand B
  //   Inputs
  //   Outputs
  //   Multiplier +-
  //   A(+) ^ B(+)
  //   A(-) ^ B(-)
  //   Operations
  //   A(+) ^ B(-)
  //   A(-) ^ B(+)
endmodule

module Divider (
  input  [31:0] A,
  input  [31:0] B,
  input  [31:0] Lo,
  output [31:0] Hi
);

  wire [31:0] _00_Hi, _00_Lo, _01_Hi, _01_Lo, _10_Hi, _10_Lo, _11_Hi, _11_Lo, divider_2_out, divider_2_rem,
       divider_3_out, divider_4_rem, negator_1_out, negator_4_out, negator_5_out, negator_6_out;

  // Probe on A
  // Probe on B
  Multiplexer #(.select(2), .width(32), .enable("false")) multiplexer_1 (
    .in0(_00_Hi), .in1(_01_Hi), .in2(_10_Hi), .in3(_11_Hi), .out(Hi), .sel({A[31], B[31]}));
  Multiplexer #(.select(2), .width(32), .enable("false")) multiplexer_2 (
    .in0(_00_Lo), .in1(_01_Lo), .in2(_10_Lo), .in3(_11_Lo), .out(Lo), .sel({A[31], B[31]}));
  // Probe on _00_Lo
  Divider_part #(.width(32)) divider_1 (.a(A), .b(B), .out(_00_Lo), .rem(_00_Hi));  // open: upper
  // Probe on _00_Hi
  Negator #(.width(32)) negator_1 (.in(A), .out(negator_1_out));
  Divider_part #(.width(32)) divider_2 (
    .a(negator_1_out), .b(B), .out(divider_2_out), .rem(divider_2_rem));  // open: upper
  Negator #(.width(32)) negator_2 (.in(divider_2_rem), .out(_10_Hi));
  // Probe on _10_Lo
  Negator #(.width(32)) negator_3 (.in(divider_2_out), .out(_10_Lo));
  // Probe on _10_Hi
  Negator #(.width(32)) negator_4 (.in(B), .out(negator_4_out));
  Negator #(.width(32)) negator_5 (.in(A), .out(negator_5_out));
  Negator #(.width(32)) negator_6 (.in(B), .out(negator_6_out));
  Divider_part #(.width(32)) divider_3 (.a(A), .b(negator_4_out), .out(divider_3_out), .rem(_01_Hi));  // open: upper
  // Probe on _01_Hi
  Divider_part #(.width(32)) divider_4 (
    .a(negator_5_out), .b(negator_6_out), .out(_11_Lo), .rem(divider_4_rem));  // open: upper
  // Probe on _01_Lo
  Negator #(.width(32)) negator_7 (.in(divider_3_out), .out(_01_Lo));
  // Probe on _11_Lo
  Negator #(.width(32)) negator_8 (.in(divider_4_rem), .out(_11_Hi));
  // Probe on _11_Hi

  // Other names for the same wires on the sheet: A_t = A[31]; B_t = B[31]

  // Notes on the sheet:
  //   Operand A
  //   Operand B
  //   Inputs
  //   Outputs
  //   Divider +-
  //   A(+) ^ B(+)
  //   A(-) ^ B(+)
  //   Operations
  //   A(+) ^ B(-)
  //   A(-) ^ B(-)
endmodule

module Register_File_2 (
  input  [4:0] in_1,
  input  [31:0] in_2,
  input  RW,
  input  [4:0] SA,
  input  [4:0] SB,
  input  in_6,
  input  in_7,
  input  in_8,
  input  in_9,
  output [31:0] A,
  output [31:0] B,
  output [31:0] SP
);

  wire _0, _4, _8, _12, _16, _20, _24, _28, or_1_out;
  wire [1:0] priority_encoder_1_out;
  wire [2:1] _28___31;
  wire [3:1] _0___3, _4___7, _8___11, _12___15, _16___19, _20___23, _24___27;
  wire [4:0] multiplexer_1_out;
  wire [31:0] adder_1_out, multiplexer_3_out, Q10, Re0, Re1, Re2, Re3, Re4, Re5, Re6, Re7, Re8, Re9, Re10,
       Re11, Re12, Re13, Re14, Re15, Re16, Re17, Re18, Re19, Re20, Re21, Re22, Re23, Re24, Re25, Re26, Re27,
       Re28, Re29, Re30, subtractor_1_out, undriven;

  Decoder #(.select(5)) decoder_1 (
    .out0(_0), .out1(_0___3[1]), .out2(_0___3[2]), .out3(_0___3[3]), .out4(_4), .out5(_4___7[1]),
    .out6(_4___7[2]), .out7(_4___7[3]), .out8(_8), .out9(_8___11[1]), .out10(_8___11[2]), .out11(_8___11[3]),
    .out12(_12), .out13(_12___15[1]), .out14(_12___15[2]), .out15(_12___15[3]), .out16(_16),
    .out17(_16___19[1]), .out18(_16___19[2]), .out19(_16___19[3]), .out20(_20), .out21(_20___23[1]),
    .out22(_20___23[2]), .out23(_20___23[3]), .out24(_24), .out25(_24___27[1]), .out26(_24___27[2]),
    .out27(_24___27[3]), .out28(_28), .out29(_28___31[1]), .out30(_28___31[2]), .out31(in_9),
    .sel(multiplexer_1_out), .en(1'b1));
  Multiplexer #(.width(5), .enable("false")) multiplexer_1 (
    .in0({5{1'b0}}), .in1(in_1), .out(multiplexer_1_out), .sel(RW));
  Multiplexer #(.select(5), .width(32), .enable("false")) multiplexer_2 (
    .in0(Re0), .in1(Re1), .in2(Re2), .in3(Re3), .in4(Re4), .in5(Re5), .in6(Re6), .in7(Re7), .in8(Re8),
    .in9(Re9), .in10(Re10), .in11(Re11), .in12(Re12), .in13(Re13), .in14(Re14), .in15(Re15), .in16(Re16),
    .in17(Re17), .in18(Re18), .in19(Re19), .in20(Re20), .in21(Re21), .in22(Re22), .in23(Re23), .in24(Re24),
    .in25(Re25), .in26(Re26), .in27(Re27), .in28(Re28), .in29(Re29), .in30(Re30), .in31(SP), .out(A), .sel(SA));
  Register #(.width(32)) register_1 (.D(in_2), .en(_0___3[1]), .Q(Re1), .clk(in_6), .clr(in_7));
  Register #(.width(32)) register_2 (.D(in_2), .en(_4___7[3]), .Q(Re7), .clk(in_6), .clr(in_7));
  Register #(.width(32)) register_3 (.D(in_2), .en(_12___15[1]), .Q(Re13), .clk(in_6), .clr(in_7));
  Register #(.width(32)) register_4 (.D(in_2), .en(_16___19[3]), .Q(Re19), .clk(in_6), .clr(in_7));
  Register #(.width(32)) register_5 (.D(in_2), .en(_24___27[1]), .Q(Re25), .clk(in_6), .clr(in_7));
  Adder #(.width(32)) adder_1 (.a(SP), .b(32'h4), .out(adder_1_out));  // open: cin, cout
  Subtractor #(.width(32)) subtractor_1 (.a(SP), .b(32'h4), .out(subtractor_1_out));  // open: bin, bout
  Register #(.width(32)) register_6 (.D(in_2), .en(_0___3[2]), .Q(Re2), .clk(in_6), .clr(in_7));
  Register #(.width(32)) register_7 (.D(in_2), .en(_8), .Q(Re8), .clk(in_6), .clr(in_7));
  Register #(.width(32)) register_8 (.D(in_2), .en(_12___15[2]), .Q(Re14), .clk(in_6), .clr(in_7));
  Register #(.width(32)) register_9 (.D(in_2), .en(_20), .Q(Re20), .clk(in_6), .clr(in_7));
  Register #(.width(32)) register_10 (.D(in_2), .en(_24___27[2]), .Q(Re26), .clk(in_6), .clr(in_7));
  Multiplexer #(.select(2), .width(32), .enable("false")) multiplexer_3 (
    .in0(in_2), .in1(adder_1_out), .in2(subtractor_1_out), .in3(32'h3ffff), .out(multiplexer_3_out),
    .sel(priority_encoder_1_out));
  Priority_Encoder #(.select(2)) priority_encoder_1 (
    .in0(1'b1), .in1(in_9), .in2(in_8), .in3(in_7), .out(priority_encoder_1_out));
  Register #(.width(32)) R31__Stack_Pointer (.D(multiplexer_3_out), .en(or_1_out), .Q(SP), .clk(in_6));  // open: clr
  or or_1 (or_1_out, in_9, in_9, in_8, in_7);
  Register #(.width(32)) register_11 (.D(in_2), .en(_0___3[3]), .Q(Re3), .clk(in_6), .clr(in_7));
  Register #(.width(32)) register_12 (.D(in_2), .en(_8___11[1]), .Q(Re9), .clk(in_6), .clr(in_7));
  Register #(.width(32)) register_13 (.D(in_2), .en(_12___15[3]), .Q(Re15), .clk(in_6), .clr(in_7));
  Register #(.width(32)) register_14 (.D(in_2), .en(_20___23[1]), .Q(Re21), .clk(in_6), .clr(in_7));
  Register #(.width(32)) register_15 (.D(in_2), .en(_24___27[3]), .Q(Re27), .clk(in_6), .clr(in_7));
  Register #(.width(32)) register_16 (.D(in_2), .en(_4), .Q(Re4), .clk(in_6), .clr(in_7));
  Register #(.width(32)) register_17 (.D(in_2), .en(_8___11[2]), .Q(Re10), .clk(in_6), .clr(in_7));
  Register #(.width(32)) register_18 (.D(in_2), .en(_16), .Q(Re16), .clk(in_6), .clr(in_7));
  Register #(.width(32)) register_19 (.D(in_2), .en(_20___23[2]), .Q(Re22), .clk(in_6), .clr(in_7));
  Register #(.width(32)) register_20 (.D(in_2), .en(_28), .Q(Re28), .clk(in_6), .clr(in_7));
  Multiplexer #(.select(5), .width(32), .enable("false")) multiplexer_4 (
    .in0(Re0), .in1(Re1), .in2(Re2), .in3(Re3), .in4(Re4), .in5(Re5), .in6(Re6), .in7(Re7), .in8(Re8),
    .in9(Re9), .in10(Q10), .in11(Re11), .in12(Re12), .in13(Re13), .in14(Re14), .in15(Re15), .in16(Re16),
    .in17(Re17), .in18(Re18), .in19(Re19), .in20(Re20), .in21(undriven), .in22(Re22), .in23(Re23),
    .in24(Re24), .in25(Re25), .in26(Re26), .in27(Re27), .in28(Re28), .in29(Re29), .in30(Re30), .in31(SP),
    .out(B), .sel(SB));
  Register #(.width(32)) register_21 (.D(in_2), .en(_4___7[1]), .Q(Re5), .clk(in_6), .clr(in_7));
  Register #(.width(32)) register_22 (.D(in_2), .en(_8___11[3]), .Q(Re11), .clk(in_6), .clr(in_7));
  Register #(.width(32)) register_23 (.D(in_2), .en(_16___19[1]), .Q(Re17), .clk(in_6), .clr(in_7));
  Register #(.width(32)) register_24 (.D(in_2), .en(_20___23[3]), .Q(Re23), .clk(in_6), .clr(in_7));
  Register #(.width(32)) register_25 (.D(in_2), .en(_28___31[1]), .Q(Re29), .clk(in_6), .clr(in_7));
  Register #(.width(32)) R0 (.D({32{1'b0}}), .Q(Re0), .clk(in_6), .clr(in_7));  // open: en
  Register #(.width(32)) register_26 (.D(in_2), .en(_4___7[2]), .Q(Re6), .clk(in_6), .clr(in_7));
  Register #(.width(32)) register_27 (.D(in_2), .en(_12), .Q(Re12), .clk(in_6), .clr(in_7));
  Register #(.width(32)) register_28 (.D(in_2), .en(_16___19[2]), .Q(Re18), .clk(in_6), .clr(in_7));
  Register #(.width(32)) register_29 (.D(in_2), .en(_24), .Q(Re24), .clk(in_6), .clr(in_7));
  Register #(.width(32)) register_30 (.D(in_2), .en(_28___31[2]), .Q(Re30), .clk(in_6), .clr(in_7));

  // Other names for the same wires on the sheet: _0___3[0] = _0; _1 = _0___3[1]; _2 = _0___3[2]; _3 = _0___3[3];
  //   _4___7[0] = _4; _5 = _4___7[1]; _6 = _4___7[2]; _7 = _4___7[3]; _8___11[0] = _8; _9 = _8___11[1];
  //   _10 = _8___11[2]; _11 = _8___11[3]; _12___15[0] = _12; _13 = _12___15[1]; _14 = _12___15[2]; _15 = _12___15[3];
  //   _16___19[0] = _16; _17 = _16___19[1]; _18 = _16___19[2]; _19 = _16___19[3]; _20___23[0] = _20;
  //   _21 = _20___23[1]; _22 = _20___23[2]; _23 = _20___23[3]; _24___27[0] = _24; _25 = _24___27[1];
  //   _26 = _24___27[2]; _27 = _24___27[3]; _28___31 (some bits) = {in_9, _28}; _29 = _28___31[1]; _30 = _28___31[2];
  //   _31 = in_9; Pop = in_9; Address[4:0] = in_1; clock = in_6; Data_A[31:0] = A; Data_B[31:0] = B;
  //   Data_input[31:0] = in_2; Push = in_8; Re31[31:0] = SP; rst = in_7; Selected_A[4:0] = SA; Selected_B[4:0] = SB

  // Notes on the sheet:
  //   Outputs
  //   Stack Pointer
  //   Inputs
  //   Read/Write
  //   Selectors
  //   Data A
  //   Data B
  //   Writing Controller
  //   Load Tunnels
  //   Reading Controllers
  //   Stack Pointer
  //   Registers (1-30)
  //   Register 0
endmodule

module Sing_Extend_2 (
  input  [15:0] in_1,
  input  Logical,
  output [31:0] Output
);

  wire [31:0] bit_extender_1_out, bit_extender_2_out;

  // Probe on in_1
  assign bit_extender_1_out = {{16{in_1[15]}}, in_1};  // Bit_Extender bit_extender_1
  assign bit_extender_2_out = {{16{1'b0}}, in_1};  // Bit_Extender bit_extender_2
  Multiplexer #(.width(32), .enable("false")) multiplexer_1 (
    .in0(bit_extender_1_out), .in1(bit_extender_2_out), .out(Output), .sel(Logical));
  // Probe on Output

  // Other names for the same wires on the sheet: Op = Logical

  // Notes on the sheet:
  //   Input
  //   Ouput
endmodule

module Control_Unit_2 (
  input  [5:0] Op_code,
  input  [5:0] Func_code,
  input  [3:0] Read_Time,
  input  [3:0] Write_Time,
  input  CLK,
  input  Reset,
  output [3:0] ALU_Op,
  output [2:0] Branch_Op,
  output Logical_Inmed_Op,
  output [2:0] Select_DI,
  output pop,
  output KBD_ENABLE,
  output TTY_ENABLE,
  output Chip_Select,
  output RW_RAM,
  output Load_PC,
  output Load_Instruction,
  output R_W,
  output rt_rd,
  output [1:0] Select_B,
  output [1:0] Select_Address,
  output Push,
  output Save_Data,
  output END
);

  wire and_2_out, CS_0, CS_1, CS_2, CS_3, CS_4, d_ff_2_q, d_ff_3_q, d_ff_8_q, demultiplexer_1_out0,
       demultiplexer_1_out1, demultiplexer_2_out0, demultiplexer_3_out0, demultiplexer_3_out4,
       demultiplexer_3_out5, demultiplexer_3_out6, demultiplexer_4_out1, demultiplexer_5_out1,
       demultiplexer_6_out0, demultiplexer_7_out0, demultiplexer_7_out1, demultiplexer_8_out0,
       demultiplexer_8_out1, demultiplexer_9_out0, demultiplexer_9_out1, demultiplexer_10_out0, IDLE_q, lw,
       nor_1_out, not_1_out, or_1_out, or_6_out, or_7_out, or_8_out, pop_t, R___W_1, R___W_2, R___W_3,
       R___W_5, R___W_6, Ram_Op1, Ram_Op2, Stack_Op1, Stack_Op2, sw, Wait, WAIT_q;
  wire [1:0] Sp_Op;
  wire [2:0] CU_Op;
  wire [3:0] counter_1_q, RT____WT;

  Demultiplexer #(.disabled(0), .enable("false")) demultiplexer_1 (
    .out0(demultiplexer_1_out0), .out1(demultiplexer_1_out1), .in(IDLE_q), .sel(not_1_out));
  D_Flip_Flop IDLE (.clk(CLK), .D(demultiplexer_1_out0), .Q(IDLE_q), .preset(Reset));  // open: Qn, en, reset
  not not_1 (not_1_out, Reset);
  or or_1 (or_1_out, demultiplexer_2_out0, d_ff_8_q, demultiplexer_1_out1);
  Operation_Decoder operation_decoder_1 (
    .Op_code(Op_code), .Func_code(Func_code), .CU_Operation(CU_Op), .Branch_Operation(Branch_Op),
    .ALU_Operation(ALU_Op), .Select_B(Select_B), .Special_Operation(Sp_Op), .Select_DI(Select_DI), .lw(lw),
    .pop(pop_t), .rt_rd(rt_rd), .Logical_Inmed_Op(Logical_Inmed_Op));
  D_Flip_Flop d_ff_1 (.clk(CLK), .D(or_1_out), .Q(CS_0), .reset(Reset));  // open: Qn, preset, en
  Demultiplexer #(.enable("false")) demultiplexer_2 (
    .out0(demultiplexer_2_out0), .out1(Load_Instruction), .in(CS_0), .sel(Wait));
  D_Flip_Flop d_ff_2 (.clk(CLK), .D(Load_Instruction), .Q(d_ff_2_q), .reset(Reset));  // open: Qn, preset, en
  Demultiplexer #(.select(3), .disabled(0), .enable("false")) demultiplexer_3 (
    .out0(demultiplexer_3_out0), .out1(R___W_1), .out2(R___W_2), .out3(R___W_3), .out4(demultiplexer_3_out4),
    .out5(demultiplexer_3_out5), .out6(demultiplexer_3_out6), .in(d_ff_2_q), .sel(CU_Op));  // open: out7
  Multiplexer #(.width(4), .enable("false")) multiplexer_1 (
    .in0(Read_Time), .in1(Write_Time), .out(RT____WT), .sel(RW_RAM));
  Demultiplexer #(.disabled(0), .enable("false")) demultiplexer_4 (
    .out0(sw), .out1(demultiplexer_4_out1), .in(demultiplexer_3_out4), .sel(lw));
  Demultiplexer #(.disabled(0), .enable("false")) demultiplexer_5 (
    .out0(Push), .out1(demultiplexer_5_out1), .in(demultiplexer_3_out5), .sel(pop_t));
  Demultiplexer #(.select(2), .disabled(0), .enable("false")) demultiplexer_6 (
    .out0(demultiplexer_6_out0), .out1(R___W_6), .out2(R___W_5), .out3(TTY_ENABLE),
    .in(demultiplexer_3_out6), .sel(Sp_Op));
  D_Flip_Flop d_ff_3 (.clk(CLK), .D(Chip_Select), .Q(d_ff_3_q), .reset(Reset));  // open: Qn, preset, en
  or or_2 (Ram_Op1, demultiplexer_7_out0, sw);
  or or_3 (Ram_Op2, demultiplexer_8_out0, demultiplexer_4_out1);
  or or_4 (Stack_Op1, demultiplexer_9_out0, Push);
  or or_5 (Stack_Op2, demultiplexer_10_out0, demultiplexer_5_out1);
  or or_6 (or_6_out, END, demultiplexer_6_out0);
  Counter #(.width(4), .max('hf)) counter_1 (
    .load(Chip_Select), .D(RT____WT), .count(d_ff_3_q), .Q(counter_1_q), .clk(CLK));  // open: carry, clr
  D_Flip_Flop d_ff_4 (.clk(CLK), .D(Ram_Op1), .Q(CS_1), .reset(Reset));  // open: Qn, preset, en
  D_Flip_Flop d_ff_5 (.clk(CLK), .D(Ram_Op2), .Q(CS_2), .reset(Reset));  // open: Qn, preset, en
  D_Flip_Flop d_ff_6 (.clk(CLK), .D(Stack_Op1), .Q(CS_4), .reset(Reset));  // open: Qn, preset, en
  D_Flip_Flop d_ff_7 (.clk(CLK), .D(Stack_Op2), .Q(CS_3), .reset(Reset));  // open: Qn, preset, en
  D_Flip_Flop u_END (.clk(CLK), .D(or_6_out), .Q(END), .en(demultiplexer_6_out0), .reset(Reset));  // open: Qn, preset
  nor nor_1 (nor_1_out, counter_1_q[0], counter_1_q[1], counter_1_q[2], counter_1_q[3]);
  and and_1 (Wait, nor_1_out, d_ff_3_q);
  Demultiplexer #(.enable("false")) demultiplexer_7 (
    .out0(demultiplexer_7_out0), .out1(demultiplexer_7_out1), .in(CS_1), .sel(Wait));
  Demultiplexer #(.enable("false")) demultiplexer_8 (
    .out0(demultiplexer_8_out0), .out1(demultiplexer_8_out1), .in(CS_2), .sel(Wait));
  Demultiplexer #(.enable("false")) demultiplexer_9 (
    .out0(demultiplexer_9_out0), .out1(demultiplexer_9_out1), .in(CS_4), .sel(Wait));
  Demultiplexer #(.enable("false")) demultiplexer_10 (.out0(demultiplexer_10_out0), .out1(pop), .in(CS_3), .sel(Wait));
  D_Flip_Flop u_WAIT (.clk(CLK), .D(TTY_ENABLE), .Q(WAIT_q), .reset(Reset));  // open: Qn, preset, en
  D_Flip_Flop WAIT_2 (.clk(CLK), .D(R___W_5), .Q(KBD_ENABLE), .reset(Reset));  // open: Qn, preset, en
  or or_7 (or_7_out, Ram_Op1, Ram_Op2);
  or or_8 (or_8_out, Stack_Op1, Stack_Op2);
  or or_9 (Chip_Select, CS_0, CS_1, CS_4, CS_2, CS_3);
  Priority_Encoder #(.select(2)) priority_encoder_1 (
    .in0(1'b1), .in1(or_7_out), .in2(or_8_out), .out(Select_Address));  // open: in3, gs, en_out, en_in
  or or_10 (Load_PC, demultiplexer_3_out0, R___W_1, R___W_2, R___W_3, demultiplexer_7_out1, demultiplexer_8_out1, demultiplexer_9_out1, pop, R___W_6, KBD_ENABLE, WAIT_q);
  and and_2 (and_2_out, R___W_1, ~ALU_Op[3]);  // AND_Gate
  D_Flip_Flop d_ff_8 (.clk(CLK), .D(Load_PC), .Q(d_ff_8_q), .reset(Reset));  // open: Qn, preset, en
  or or_11 (RW_RAM, CS_1, CS_4);
  or or_12 (R_W, and_2_out, R___W_2, R___W_3, CS_2, CS_3, R___W_5, R___W_6);
  or or_13 (Save_Data, sw, Push);

  // Other names for the same wires on the sheet: Hi_Lo_Op = ALU_Op[3]; CS = Chip_Select; Load_Inst = Load_Instruction;
  //   R___W_7 = CS_2; R_W_RAM_1 = CS_1; RT[3:0] = Read_Time; S_pop = pop; R_W_RAM_2 = CS_4; Stack_Op_1 = CS_4;
  //   R___W_4 = CS_3; Stack_Op_2 = CS_3; WT[3:0] = Write_Time

  // Notes on the sheet:
  //   Inputs
  //   Outputs
  //   Op/Func Decode
  //   Inmediate Operation
  //   Register Operation
  //   RAM Operation
  //   Stack Operation
  //   Special Operation
  //   Branch Operation
  //   ALU Operation
  //   Wait
  //   Store word
  //   Load word
  //   Push
  //   Pop
  //   Disjunction
endmodule

module Operation_Decoder (
  input  [5:0] Op_code,
  input  [5:0] Func_code,
  output [2:0] CU_Operation,
  output [2:0] Branch_Operation,
  output [3:0] ALU_Operation,
  output [1:0] Select_B,
  output [1:0] Special_Operation,
  output [2:0] Select_DI,
  output lw,
  output pop,
  output rt_rd,
  output Logical_Inmed_Op
);

  wire add, addi, AL_Op, \and , and_5_out, and_7_out, and_9_out, and_11_out, and_13_out, and_15_out,
       and_17_out, and_18_out, and_19_out, and_20_out, and_21_out, and_22_out, and_35_out, and_36_out,
       and_37_out, and_44_out, and_49_out, and_50_out, and_55_out, and_56_out, and_57_out, and_58_out,
       and_63_out, andi, B_Jump, beq, bgtz, blez, bltz, bne, Branch_Op, div, divu, F_000000, halt, Inmed_Op,
       j, jr, kbd, mfhi, mflo, mult, Mult_Div_Op, mulu, nop, \nor , O_000000, O_111000, O_111111, \or ,
       or_10_out, or_11_out, or_12_out, or_13_out, or_14_out, or_15_out, or_16_out, or_17_out, or_18_out,
       or_19_out, or_20_out, ori, push, RAM_Op, Register_Op, rnd, sliti, slitiu, slt, sltu, Special_Op,
       Stack_Op, sub, sw, tty, \xor , xori;

  and and_1 (O_000000, ~Op_code[0], ~Op_code[1], ~Op_code[2], ~Op_code[3], ~Op_code[4], ~Op_code[5]);  // AND_Gate
  and and_2 (O_111000, ~Op_code[0], ~Op_code[1], ~Op_code[2], Op_code[3], Op_code[4], Op_code[5]);  // AND_Gate
  and and_3 (O_111111, Op_code[0], Op_code[1], Op_code[2], Op_code[3], Op_code[4], Op_code[5]);
  and and_4 (F_000000, ~Func_code[0], ~Func_code[1], ~Func_code[2], ~Func_code[3], ~Func_code[4], ~Func_code[5]);  // AND_Gate
  and and_5 (and_5_out, ~Func_code[0], ~Func_code[1], ~Func_code[2], ~Func_code[3], ~Func_code[4], Func_code[5]);  // AND_Gate
  and and_6 (add, and_5_out, O_000000);
  and and_7 (and_7_out, ~Func_code[0], Func_code[1], ~Func_code[2], ~Func_code[3], ~Func_code[4], Func_code[5]);  // AND_Gate
  and and_8 (sub, and_7_out, O_000000);
  and and_9 (and_9_out, ~Func_code[0], ~Func_code[1], ~Func_code[2], Func_code[3], Func_code[4], ~Func_code[5]);  // AND_Gate
  and and_10 (mult, and_9_out, O_000000);
  and and_11 (and_11_out, Func_code[0], ~Func_code[1], ~Func_code[2], Func_code[3], Func_code[4], ~Func_code[5]);  // AND_Gate
  and and_12 (mulu, and_11_out, O_000000);
  and and_13 (and_13_out, ~Func_code[0], Func_code[1], ~Func_code[2], Func_code[3], Func_code[4], ~Func_code[5]);  // AND_Gate
  and and_14 (div, and_13_out, O_000000);
  and and_15 (and_15_out, Func_code[0], Func_code[1], ~Func_code[2], Func_code[3], Func_code[4], ~Func_code[5]);  // AND_Gate
  and and_16 (divu, and_15_out, O_000000);
  and and_17 (and_17_out, ~Func_code[0], Func_code[1], ~Func_code[2], Func_code[3], ~Func_code[4], Func_code[5]);  // AND_Gate
  and and_18 (and_18_out, Func_code[0], Func_code[1], ~Func_code[2], Func_code[3], ~Func_code[4], Func_code[5]);  // AND_Gate
  and and_19 (and_19_out, ~Func_code[0], ~Func_code[1], Func_code[2], ~Func_code[3], ~Func_code[4], Func_code[5]);  // AND_Gate
  and and_20 (and_20_out, Func_code[0], ~Func_code[1], Func_code[2], ~Func_code[3], ~Func_code[4], Func_code[5]);  // AND_Gate
  and and_21 (and_21_out, Func_code[0], Func_code[1], Func_code[2], ~Func_code[3], ~Func_code[4], Func_code[5]);  // AND_Gate
  and and_22 (and_22_out, ~Func_code[0], ~Func_code[1], ~Func_code[2], Func_code[3], ~Func_code[4], Func_code[5]);  // AND_Gate
  and and_23 (slt, and_17_out, O_000000);
  and and_24 (sltu, and_18_out, O_000000);
  and and_25 (\and , and_19_out, O_000000);
  and and_26 (\or , and_20_out, O_000000);
  and and_27 (\nor , and_21_out, O_000000);
  and and_28 (\xor , and_22_out, O_000000);
  and and_29 (addi, ~Op_code[0], ~Op_code[1], ~Op_code[2], Op_code[3], ~Op_code[4], ~Op_code[5]);  // AND_Gate
  and and_30 (sliti, ~Op_code[0], Op_code[1], ~Op_code[2], Op_code[3], ~Op_code[4], ~Op_code[5]);  // AND_Gate
  and and_31 (slitiu, Op_code[0], Op_code[1], ~Op_code[2], Op_code[3], ~Op_code[4], ~Op_code[5]);  // AND_Gate
  and and_32 (andi, ~Op_code[0], ~Op_code[1], Op_code[2], Op_code[3], ~Op_code[4], ~Op_code[5]);  // AND_Gate
  and and_33 (ori, Op_code[0], ~Op_code[1], Op_code[2], Op_code[3], ~Op_code[4], ~Op_code[5]);  // AND_Gate
  and and_34 (xori, ~Op_code[0], Op_code[1], Op_code[2], Op_code[3], ~Op_code[4], ~Op_code[5]);  // AND_Gate
  and and_35 (and_35_out, ~Func_code[0], ~Func_code[1], ~Func_code[2], Func_code[3], ~Func_code[4], ~Func_code[5]);  // AND_Gate
  and and_36 (and_36_out, ~Func_code[0], ~Func_code[1], ~Func_code[2], ~Func_code[3], Func_code[4], ~Func_code[5]);  // AND_Gate
  and and_37 (and_37_out, ~Func_code[0], Func_code[1], ~Func_code[2], ~Func_code[3], Func_code[4], ~Func_code[5]);  // AND_Gate
  and and_38 (beq, ~Op_code[0], ~Op_code[1], Op_code[2], ~Op_code[3], ~Op_code[4], ~Op_code[5]);  // AND_Gate
  and and_39 (bne, Op_code[0], ~Op_code[1], Op_code[2], ~Op_code[3], ~Op_code[4], ~Op_code[5]);  // AND_Gate
  and and_40 (blez, ~Op_code[0], Op_code[1], Op_code[2], ~Op_code[3], ~Op_code[4], ~Op_code[5]);  // AND_Gate
  and and_41 (bgtz, Op_code[0], Op_code[1], Op_code[2], ~Op_code[3], ~Op_code[4], ~Op_code[5]);  // AND_Gate
  and and_42 (bltz, Op_code[0], ~Op_code[1], ~Op_code[2], ~Op_code[3], ~Op_code[4], ~Op_code[5]);  // AND_Gate
  and and_43 (j, ~Op_code[0], Op_code[1], ~Op_code[2], ~Op_code[3], ~Op_code[4], ~Op_code[5]);  // AND_Gate
  and and_44 (and_44_out, ~Op_code[0], ~Op_code[1], ~Op_code[2], ~Op_code[3], ~Op_code[4], ~Op_code[5]);  // AND_Gate
  and and_45 (jr, and_35_out, O_000000);
  and and_46 (mfhi, and_36_out, O_000000);
  and and_47 (mflo, and_37_out, O_000000);
  and and_48 (nop, and_44_out, F_000000);
  and and_49 (and_49_out, ~Func_code[0], ~Func_code[1], ~Func_code[2], ~Func_code[3], ~Func_code[4], ~Func_code[5]);  // AND_Gate
  and and_50 (and_50_out, Func_code[0], ~Func_code[1], ~Func_code[2], ~Func_code[3], ~Func_code[4], ~Func_code[5]);  // AND_Gate
  and and_51 (lw, Op_code[0], Op_code[1], ~Op_code[2], ~Op_code[3], ~Op_code[4], Op_code[5]);  // AND_Gate
  and and_52 (sw, Op_code[0], Op_code[1], ~Op_code[2], Op_code[3], ~Op_code[4], Op_code[5]);  // AND_Gate
  and and_53 (pop, and_49_out, O_111000);
  and and_54 (push, and_50_out, O_111000);
  and and_55 (and_55_out, Func_code[0], Func_code[1], Func_code[2], Func_code[3], Func_code[4], Func_code[5]);
  and and_56 (and_56_out, ~Func_code[0], Func_code[1], ~Func_code[2], ~Func_code[3], ~Func_code[4], ~Func_code[5]);  // AND_Gate
  and and_57 (and_57_out, ~Func_code[0], ~Func_code[1], Func_code[2], ~Func_code[3], ~Func_code[4], ~Func_code[5]);  // AND_Gate
  and and_58 (and_58_out, Func_code[0], ~Func_code[1], ~Func_code[2], ~Func_code[3], ~Func_code[4], ~Func_code[5]);  // AND_Gate
  and and_59 (halt, and_55_out, O_111111);
  and and_60 (rnd, and_56_out, O_111111);
  and and_61 (kbd, and_57_out, O_111111);
  and and_62 (tty, and_58_out, O_111111);
  or or_1 (Logical_Inmed_Op, andi, ori, xori);
  or or_2 (Special_Op, halt, rnd, kbd, tty);
  or or_3 (Stack_Op, pop, push);
  or or_4 (RAM_Op, lw, sw);
  or or_5 (Register_Op, mfhi, mflo);
  or or_6 (Mult_Div_Op, mult, mulu, div, divu);
  or or_7 (AL_Op, add, sub, mult, mulu, div, divu, slt, sltu, \and , \or , \nor , \xor );
  or or_8 (Branch_Op, nop, beq, bne, blez, bgtz, bltz, j, jr);
  or or_9 (Inmed_Op, addi, sliti, slitiu, andi, ori, xori);
  or or_10 (or_10_out, RAM_Op, add, addi);
  or or_11 (or_11_out, sub, B_Jump);
  or or_12 (or_12_out, \and , andi);
  or or_13 (or_13_out, \or , ori);
  or or_14 (or_14_out, \xor , xori);
  or or_15 (or_15_out, slt, sliti);
  or or_16 (or_16_out, sltu, slitiu);
  or or_17 (or_17_out, blez, bgtz, bltz);
  or or_18 (or_18_out, RAM_Op, Inmed_Op);
  or or_19 (or_19_out, lw, pop);
  and and_63 (and_63_out, ~AL_Op, ~Inmed_Op, ~B_Jump, ~RAM_Op);  // AND_Gate
  Priority_Encoder #(.disabled(0)) priority_encoder_1 (
    .in0(Branch_Op), .in1(AL_Op), .in2(Inmed_Op), .in3(Register_Op), .in4(RAM_Op), .in5(Stack_Op),
    .in6(Special_Op), .out(CU_Operation), .en_in(1'b1));  // open: in7, gs, en_out
  Priority_Encoder #(.select(4), .disabled(0)) priority_encoder_2 (
    .in0(or_10_out), .in1(or_11_out), .in2(or_12_out), .in3(or_13_out), .in4(\nor ), .in5(or_14_out),
    .in6(or_15_out), .in7(or_16_out), .in8(mult), .in9(mulu), .in10(div), .in11(divu), .in15(and_63_out),
    .out(ALU_Operation), .en_in(1'b1));  // open: in12, in13, in14, gs, en_out
  Priority_Encoder #(.select(2), .disabled(0)) priority_encoder_3 (
    .in0(1'b1), .in1(or_17_out), .in2(or_18_out), .out(Select_B));  // open: in3, gs, en_out, en_in
  Priority_Encoder #(.disabled(0)) priority_encoder_4 (
    .in0(1'b1), .in1(or_19_out), .in2(mfhi), .in3(mflo), .in4(kbd), .in5(rnd), .out(Select_DI));  // open: in6, in7, en_in, gs, en_out
  or or_20 (or_20_out, halt, 1'b1);
  Priority_Encoder #(.disabled(0)) priority_encoder_5 (
    .in0(1'b1), .in1(beq), .in2(bne), .in3(blez), .in4(bgtz), .in5(bltz), .in6(j), .in7(jr),
    .out(Branch_Operation), .en_in(1'b1));  // open: gs, en_out
  or or_21 (B_Jump, beq, bne, blez, bgtz, bltz);
  Priority_Encoder #(.select(2), .disabled(0)) priority_encoder_6 (
    .in0(or_20_out), .in1(rnd), .in2(kbd), .in3(tty), .out(Special_Operation), .en_in(1'b1));  // open: gs, en_out
  or or_22 (rt_rd, O_000000, O_111111, O_111000);

  // Notes on the sheet:
  //   Códigos
  //   para instrucciones de tipo R
  //   No Operation
  //   ALU
  //   ALU
  //   Func-code
  //   Register
  //   Op-code
  //   Branch
  //   RAM
  //   Stack
  //   Special
  //   Operaciones
  //   Control Unit
  //   ALU
  //   Output / Encode op
  //   Branch
  //   Special
  //   Otras
endmodule

module Branch_Control_2 (
  input  [31:0] PC_in,
  input  [31:0] RS,
  input  [31:0] \const ,
  input  [25:0] Jump,
  input  [2:0] Branch_Op,
  input  ZF,
  input  NF,
  output [31:0] PC_Out
);

  wire and_1_out, and_2_out, and_3_out, and_4_out, and_5_out, b_jump, beq, bgtz, blez, bltz, bne, j, jr, nop,
       Rs_____0;
  wire [1:0] jump_t;
  wire [31:0] Branch, multiplier_1_out, Std;
  wire [31:28] J_PC;

  Decoder #(.select(3), .disabled(0), .enable("false")) decoder_1 (
    .out0(nop), .out1(beq), .out2(bne), .out3(blez), .out4(bgtz), .out5(bltz), .out6(j), .out7(jr),
    .sel(Branch_Op));
  or or_1 (Rs_____0, ZF, NF);
  and and_1 (and_1_out, beq, ZF);
  and and_2 (and_2_out, bne, ~ZF);  // AND_Gate
  and and_3 (and_3_out, blez, Rs_____0);
  and and_4 (and_4_out, bgtz, ~Rs_____0);  // AND_Gate
  and and_5 (and_5_out, bltz, NF);
  or or_2 (b_jump, and_1_out, and_2_out, and_3_out, and_4_out, and_5_out);
  Priority_Encoder #(.select(2)) priority_encoder_1 (
    .in0(1'b1), .in1(b_jump), .in2(j), .in3(jr), .out(jump_t), .en_in(1'b1));  // open: gs, en_out
  Adder #(.width(32)) adder_1 (.a(PC_in), .b(32'h4), .out(Std));  // open: cin, cout
  Multiplier_part #(.width(32)) multiplier_1 (.a(32'h4), .b(\const ), .out(multiplier_1_out));  // open: cin, cout
  Adder #(.width(32)) adder_2 (.a(Std), .b(multiplier_1_out), .out(Branch));  // open: cin, cout
  BitSelector #(.width(32), .group(4)) bitselector_1 (.in(PC_in), .out(J_PC), .sel(3'b111));
  // Probe on nothing
  Multiplexer #(.select(2), .width(32), .disabled(0), .enable("false")) multiplexer_1 (
    .in0(Std), .in1(Branch), .in2({J_PC, Jump, 2'b00}), .in3(RS), .out(PC_Out), .sel(jump_t));

  // Other names for the same wires on the sheet: J_PC[27:2] = Jump

  // Notes on the sheet:
  //   Input
  //   Op Decode
  //   B Jump
  //   Jump Encode
  //   Branch Value
  //   Standard Value
  //   J Jump
  //   Seleccionar Salto
  //   Output
endmodule

module Instruction_Decoder_2 (
  input  [31:0] Instruction,
  input  Load_Inst,
  input  Clock,
  input  Reset,
  output [4:0] DA,
  output [25:0] Address,
  output [4:0] SA,
  output [15:0] offset,
  output [4:0] SB,
  output [5:0] Func_code,
  output [5:0] Op_code
);

  Register #(.width(32)) Current_Instruction (
    .D(Instruction), .en(Load_Inst), .Q({Op_code, Address}), .clk(Clock), .clr(Reset));

  assign DA = Address[15:11];
  assign Func_code = Address[5:0];
  assign offset = Address[15:0];
  assign SA = Address[25:21];
  assign SB = Address[20:16];

  // Other names for the same wires on the sheet: inmediate[15:0] = Address[15:0]; rd[4:0] = Address[15:11];
  //   rt[4:0] = Address[20:16]; rs[4:0] = Address[25:21]; clk = Clock; Inst[31:0] = Instruction; rst = Reset

  // Notes on the sheet:
  //   Input
  //   Data Address
  //   Selector A
  //   Selector B
  //   Op-Code
  //   Output
  //   Dirección para instrucciones de salto
  //   Offset
  //   Func-Code
endmodule

module RAM_Manager_2 (
  input  [31:0] in_1,
  input  clk,
  input  save_data,
  input  rst,
  input  [31:0] RAM_O0,
  input  [31:0] RAM_O1,
  input  [31:0] RAM_In,
  input  [31:0] RAM_O2,
  input  [31:0] RAM_O3,
  output [3:0] Mask,
  output [15:0] Address_Out,
  output [31:0] RAM_O0_2,
  output [31:0] RAM_O1_2,
  output [31:0] RAM_Out,
  output [31:0] RAM_O2_2,
  output [31:0] RAM_O3_2
);

  wire [1:0] Bank;
  wire [15:2] divider_1_rem;
  wire [31:0] shifter_1_out;

  Shifter #(.width(32), .shift("lr")) shifter_1 (.in(in_1), .\dist (5'b00010), .out(shifter_1_out));
  Divider_part #(.width(16)) divider_1 (
    .a(shifter_1_out[15:0]), .b(16'h4), .out(Address_Out), .rem({divider_1_rem, Bank}));  // open: upper
  Multiplexer #(.select(2), .width(32), .enable("false")) multiplexer_1 (
    .in0(RAM_O0), .in1(RAM_O1), .in2(RAM_O2), .in3(RAM_O3),
    .out({RAM_Out[7:0], RAM_Out[15:8], RAM_Out[23:16], RAM_Out[31:24]}), .sel(Bank));
  Decoder #(.select(2), .enable("false")) decoder_1 (
    .out0(Mask[0]), .out1(Mask[1]), .out2(Mask[2]), .out3(Mask[3]), .sel(Bank));
  Register #(.width(32)) register_1 (
    .D(RAM_In), .en(save_data), .Q({RAM_O0_2[7:0], RAM_O0_2[15:8], RAM_O0_2[23:16], RAM_O0_2[31:24]}),
    .clk(clk), .clr(rst));

  assign RAM_O1_2 = RAM_O0_2;
  assign RAM_O2_2 = RAM_O0_2;
  assign RAM_O3_2 = RAM_O0_2;

  // Notes on the sheet:
  //   Address In
endmodule
